# Fritzing sketch schema (saved by Fritzing 0.9.3b)
breadboards: 1

parts:
  Composant1 = Arduino Uno (Rev3) - ICSP
  VCC1 = Battery block 9V
  LED4 = smd LED [color="Red (633nm)" package="0603 [SMD]"]
  R1 = Resistor [tolerance=±5% resistance=220 package="0402 [SMD]"]
  R2 = Resistor [tolerance=±5% resistance=220 package="0402 [SMD]"]
  R3 = Resistor [tolerance=±5% resistance=220 package="0402 [SMD]"]
  R4 = Resistor [tolerance=±5% resistance=220 package="0402 [SMD]"]
  LED5 = smd LED [color="Red (633nm)" package="0603 [SMD]"]
  LED6 = smd LED [color="Red (633nm)" package="0603 [SMD]"]
  LED7 = smd LED [color="Red (633nm)" package="0603 [SMD]"]

nets:
  N1: Composant1.ICSP_MOSI, Composant1.D11_PWM/MOSI, R4.Pin_1
  N2: Composant1.GND, VCC1.-, LED4.cathode, LED5.cathode, LED6.cathode, LED7.cathode
  N3: Composant1.D9_PWM, R3.Pin_1
  N4: Composant1.D3_PWM, R1.Pin_1
  N5: Composant1.D5_PWM, R2.Pin_1
  N6: Composant1.VIN, VCC1.+
  N7: LED4.anode, R4.Pin_0
  N8: R1.Pin_0, LED7.anode
  N9: R2.Pin_0, LED6.anode
  N10: R3.Pin_0, LED5.anode

// code stored in the sketch: code.ino

int maximum = 255; //Valeur maximum des leds (MAX: 255)
int minimum = 100; //Valeur minimum des leds (MIN: 0)

int changeSpeed = 100; //Délais d'attente en ms

int leds[] = {3, 5, 9, 11}; //Mettre tous les numéros de pin pour les leds ici

void setup() {
  for(int led : leds)
    pinMode(led, OUTPUT);
}

void loop() {
  for(int led : leds)
    analogWrite(led, random(minimum, maximum));  
  delay(changeSpeed);
}
